# Fritzing sketch lolin_d32_pro (saved by Fritzing 0.9.4)
breadboards: 1

parts:
  MCU1 = Wemos Lolin32lite
  M1 = bn-220- GPS-module
  BAT1 = Battery Holders [package=lipo-1100mAh]
  Power_(SPST) = SPST Switch [package=switch-spdt_kit]
  WIFI = LEDs [package=led10mm]
  ACTIVE = LEDs [package=led10mm]
  47_Ohm = Resistor [tolerance=±5% resistance=220 package="0402 [SMD]"]
  47_Ohm_2 = Resistor [tolerance=±5% resistance=220 package="2512 [SMD]"]
  WiFi_(momentary) = SPST Switch [package=switch-spdt_kit]

nets:
  N1: MCU1.pin_1, M1.pin_4
  N2: MCU1.pin_2, Power_(SPST).S
  N3: MCU1.pin_9, WiFi_(momentary).O
  N4: MCU1.pin_12, 47_Ohm.Pin_1
  N5: MCU1.pin_13, 47_Ohm_2.Pin_1
  GND: MCU1.pin_15, MCU1.pin_18, MCU1.pin_21, MCU1.pin_34, M1.pin_1, BAT1.-, Power_(SPST).P, WIFI.C, ACTIVE.C, WiFi_(momentary).P
  N6: MCU1.pin_17, BAT1.+
  N7: MCU1.pin_23, M1.pin_3
  N8: MCU1.pin_25, M1.pin_2

custom parts:
  Wemos Lolin32lite: Wemos Lolin32 pro wifi and blue tooth board based on the ESP-32 cpu, digital I/Os 22, analog inputs 6, analog outputs 2, clock 240mhz, Flash 4Mbytes, PSRAM 4MB, microSD card slot, lipo battery charger (500ma connection broken out on breadboard but not pcb), usb.
  bn-220- GPS-module: bn-220l GPS module. Chipset : 8030-KT Receiving Format : GPS,GLONASS,Galileo,BeiDou,QZSS and SBAS
